// Logisim project GUESS THE NUMBER XTREME.circ as structural Verilog: 17 circuits, main circuit PROJETO 2 - PRINCIPAL
module PROJETO_2___PRINCIPAL (
  input  in_1,
  input  in_2,
  input  in_3,
  input  in_4,
  input  in_5,
  input  in_6,
  input  in_7,
  input  in_8,
  input  PAUSE,
  input  PAUSE_2,
  input  MODE,
  output out_12,
  output out_13
);

  wire A_JOGANDO, A_VENCEU, ACERTOU, and_1_out, and_3_out, and_6_out, and_8_out, and_10_out, and_12_out,
       and_14_out, B_JOGANDO, B_VENCEU, CHUTANDO__X, CHUTANDO_Y, CHUTAR, clock_1_out, clock_2_out,
       CONFIGURAR, core_2_1_a_ganhou, core_2_1_a_jog, core_2_1_acertou, core_2_1_b_ganhou, core_2_1_b_jog,
       core_2_1_empate, core_2_1_igual_cords, counter_1_q, counter_2_q, d_ff_1_q, dma, dmb_t, dsa, dsb_t,
       EMPATE, FIM_DE_JOGO, IGUAL, MAIOR, MENOR, not_1_out, or_1_out, or_2_out, or_3_out, or_4_out, or_5_out,
       or_6_out, or_7_out, or_8_out, or_9_out, \PROXÍMO , RESET, START, SX, SX2, SY, SY2, tunnel, uma, umb_t,
       usa, usb_t;
  wire [3:0] DM, DMB, DS, DSB, PA, PB, UM, UMB, US, USB, XH, XS, YH, YS;

  Counter #(.width(1), .max('h1)) counter_1 (.Q(counter_1_q), .clk(START));  // open: load, D, count, carry, clr
  Button button_1 (.out(dma));
  Button button_2 (.out(uma));
  Hex_Digit_Display hex_digit_display_1 (.value(UM));  // open: dp
  Hex_Digit_Display hex_digit_display_2 (.value(DM));  // open: dp
  or or_1 (or_1_out, dmb_t, dma);
  or or_2 (or_2_out, uma, umb_t);
  or or_3 (or_3_out, counter_1_q, 1'b1);
  Hex_Digit_Display hex_digit_display_3 (.value(PA));  // open: dp
  LED led_1 (.in(1'b1));
  LED led_2 (.in(1'b1));
  _7_Segment_Display u_7_segment_display_1 (.g(SX2));  // open: f, a, b, e, d, c, dp
  Hex_Digit_Display hex_digit_display_4 (.value(XS));  // open: dp
  LED led_3 (.in(A_JOGANDO));
  or or_4 (or_4_out, dsa, dsb_t);
  D_Flip_Flop d_ff_1 (.clk(START), .D(or_3_out), .Q(d_ff_1_q));  // open: Qn, preset, en, reset
  Button button_3 (.out(dsa));
  Button button_4 (.out(usa));
  Hex_Digit_Display hex_digit_display_5 (.value(US));  // open: dp
  Hex_Digit_Display hex_digit_display_6 (.value(DS));  // open: dp
  CRONOMETRO cronometro_1 (
    .RESET(RESET), .MODE(tunnel), .DM_2(DM), .UM_2(UM), .DS_2(DS), .US_2(US), .END(out_12), .PAUSE(PAUSE),
    .CLOCK_PRINCIPAL(and_6_out), .dm(or_1_out), .um(or_2_out), .ds(or_4_out), .us(or_5_out));
  or or_5 (or_5_out, usa, usb_t);
  and and_1 (and_1_out, d_ff_1_q, clock_1_out);
  Clock clock_1 (.out(clock_1_out));
  and and_2 (B_VENCEU, core_2_1_b_ganhou, FIM_DE_JOGO);
  TABELA_VERDADE tabela_verdade_1 (
    .a(in_1), .c(in_2), .e(in_3), .f(in_4), .saida(SX2), .h(XS[3]), .i(XS[2]), .j(XS[1]), .k(XS[0]));
  Button button_5 (.out(START));
  _7_Segment_Display u_7_segment_display_2 (.g(SX));  // open: f, a, b, e, d, c, dp
  and and_3 (and_3_out, out_12, d_ff_1_q);
  and and_4 (A_VENCEU, core_2_1_a_ganhou, FIM_DE_JOGO);
  and and_5 (EMPATE, core_2_1_empate, FIM_DE_JOGO);
  LED led_4 (.in(A_VENCEU));
  LED led_5 (.in(MAIOR));
  Button button_6 (.out(\PROXÍMO ));
  Hex_Digit_Display hex_digit_display_7 (.value(XH));  // open: dp
  LED led_6 (.in(CHUTANDO__X));
  and and_6 (and_6_out, core_2_1_a_jog, and_1_out);
  LED led_7 (.in(FIM_DE_JOGO));
  LED led_8 (.in(EMPATE));
  LED led_9 (.in(tunnel));
  Button button_7 (.out(CONFIGURAR));
  LED led_10 (.in(ACERTOU));
  LED led_11 (.in(IGUAL));
  Button button_8 (.out(CHUTAR));
  _7_Segment_Display u_7_segment_display_3 (.g(SY));  // open: f, a, b, e, d, c, dp
  LED led_12 (.in(CHUTANDO_Y));
  and and_7 (FIM_DE_JOGO, and_3_out, and_8_out);
  and and_8 (and_8_out, d_ff_1_q, out_13);
  LED led_13 (.in(B_VENCEU));
  Button button_9 (.out(RESET));
  LED led_14 (.in(MENOR));
  Hex_Digit_Display hex_digit_display_8 (.value(YH));  // open: dp
  or or_6 (or_6_out, dma, dmb_t);
  or or_7 (or_7_out, umb_t, uma);
  CORE_2 core_2_1 (
    .A(in_1), .A2(in_2), .A3(in_3), .A4(in_4), .B(in_5), .B2(in_6), .B3(in_7), .B4(in_8),
    .B_JOG(core_2_1_b_jog), .A_JOG(core_2_1_a_jog), .CLOCK(and_10_out), .CHUTANDO_Y(CHUTANDO_Y),
    .CHUTANDO_X(CHUTANDO__X), .MUDAR_ESTADO(\PROXÍMO ), .MAIOR(MAIOR), .IGUAL_SOMA(IGUAL), .MENOR(MENOR),
    .IGUAL_CORDS(core_2_1_igual_cords), .ACERTOU(core_2_1_acertou), .RESET(RESET), .SLA_A(XH), .SLA_B(YH),
    .NEG_A(SX), .NEG_B(SY), .PLACAR_B(PB), .PLACAR_A(PA), .B_GANHOU(core_2_1_b_ganhou),
    .EMPATE(core_2_1_empate), .A_GANHOU(core_2_1_a_ganhou));
  Button button_10 (.out(umb_t));
  Button button_11 (.out(dmb_t));
  Hex_Digit_Display hex_digit_display_9 (.value(DMB));  // open: dp
  Hex_Digit_Display hex_digit_display_10 (.value(UMB));  // open: dp
  _7_Segment_Display u_7_segment_display_4 (.g(SY2));  // open: f, a, b, e, d, c, dp
  or or_8 (or_8_out, dsb_t, dsa);
  and and_9 (ACERTOU, core_2_1_igual_cords, core_2_1_acertou);
  and and_10 (and_10_out, d_ff_1_q, CHUTAR);
  TABELA_VERDADE tabela_verdade_2 (
    .a(in_5), .c(in_6), .e(in_7), .f(in_8), .saida(SY2), .h(YS[3]), .i(YS[2]), .j(YS[1]), .k(YS[0]));
  Hex_Digit_Display hex_digit_display_11 (.value(PB));  // open: dp
  Button button_12 (.out(dsb_t));
  LED led_15 (.in(1'b1));
  LED led_16 (.in(1'b1));
  Hex_Digit_Display hex_digit_display_12 (.value(DSB));  // open: dp
  Hex_Digit_Display hex_digit_display_13 (.value(YS));  // open: dp
  LED led_17 (.in(B_JOGANDO));
  or or_9 (or_9_out, usb_t, usa);
  and and_11 (A_JOGANDO, d_ff_1_q, core_2_1_a_jog);
  Button button_13 (.out(usb_t));
  Hex_Digit_Display hex_digit_display_14 (.value(USB));  // open: dp
  CRONOMETRO cronometro_2 (
    .RESET(RESET), .MODE(tunnel), .DM_2(DMB), .UM_2(UMB), .DS_2(DSB), .US_2(USB), .END(out_13),
    .PAUSE(PAUSE_2), .CLOCK_PRINCIPAL(and_12_out), .dm(or_6_out), .um(or_7_out), .ds(or_8_out), .us(or_9_out));
  and and_12 (and_12_out, core_2_1_b_jog, and_14_out);
  Counter #(.width(1), .max('h1)) counter_2 (.Q(counter_2_q), .clk(CONFIGURAR));  // open: load, D, count, carry, clr
  and and_13 (B_JOGANDO, d_ff_1_q, core_2_1_b_jog);
  and and_14 (and_14_out, d_ff_1_q, clock_2_out);
  D_Flip_Flop d_ff_2 (.clk(CONFIGURAR), .D(not_1_out), .Q(tunnel));  // open: Qn, preset, en, reset
  not not_1 (not_1_out, counter_2_q);
  Clock clock_2 (.out(clock_2_out));

  // Other names for the same wires on the sheet: A = in_1; A2 = in_2; A3 = in_3; A4 = in_4; B = in_5; B2 = in_6;
  //   B3 = in_7; B4 = in_8

  // Notes on the sheet:
  //   JOGADOR - A
  //   ____
  //   GUESS THE NUMBER
  //   GUESS THE NUMBER
  //   ________________________________
  //   ___________________________________________
  //   SISTEMA DO GAME
  //   XTREME
  //   ____
  //   JOGADOR - B
endmodule

module FLIP_FLOP_D (
  input  D,
  input  CLK,
  input  ENABLE,
  output out_4,
  output out_5
);

  wire and_1_out, and_2_out, and_3_out, not_1_out, not_2_out, not_3_out, not_4_out;

  not not_1 (not_1_out, not_2_out);
  not not_2 (not_2_out, CLK);
  not not_3 (not_3_out, not_1_out);
  and and_1 (and_1_out, not_3_out, ENABLE);
  not not_4 (not_4_out, D);
  and and_2 (and_2_out, D, and_1_out);
  and and_3 (and_3_out, and_1_out, not_4_out);
  nor nor_1 (out_4, and_2_out, out_5);
  nor nor_2 (out_5, out_4, and_3_out);
endmodule

module CONTADOR_DE_0_9 (
  input  CLK,
  input  RESET,
  input  MODE,
  output [3:0] SAIDA,
  output CLOCK_SEGUINTE
);

  wire and_1_out, not_1_out, not_2_out, not_3_out, not_4_out, not_5_out, or_1_out;
  wire [3:0] adder_1_out;

  REGISTRADOR_0_9 REGISTRADOR (
    .CLK(CLK), .RESET(or_1_out), .ENTRADA_4BITS(adder_1_out), .\SAÍDA_4BITS (SAIDA), .PRESET(not_4_out));
  buf or_1 (or_1_out, RESET);  // OR_Gate
  Hex_Digit_Display hex_digit_display_1 (.value(SAIDA));  // open: dp
  Adder #(.width(4)) adder_1 (.a(SAIDA), .b(4'b1111), .out(adder_1_out));  // open: cin, cout
  and and_1 (and_1_out, SAIDA[0], SAIDA[1], SAIDA[2], SAIDA[3]);
  not not_1 (not_1_out, and_1_out);
  not not_2 (not_2_out, not_1_out);
  not not_3 (not_3_out, not_2_out);
  not not_4 (not_4_out, not_3_out);
  and and_2 (CLOCK_SEGUINTE, not_4_out, not_5_out);
  not not_5 (not_5_out, MODE);
endmodule

module A (
  input  in_1
);

  wire clock_1_out;
  wire [3:0] contador_0_5_1_p2, contador_de_0_9_1_saida;

  Hex_Digit_Display hex_digit_display_1 (.value(contador_0_5_1_p2));  // open: dp
  // CONTADOR_0_5 contador_0_5_1: pin names not known; wires that end beside it: in_1, contador_0_5_1_p2
  Hex_Digit_Display hex_digit_display_2 (.value(contador_de_0_9_1_saida));  // open: dp
  Clock clock_1 (.out(clock_1_out));
  CONTADOR_DE_0_9 contador_de_0_9_1 (
    .CLK(clock_1_out), .RESET(in_1), .CLOCK_SEGUINTE(in_1), .SAIDA(contador_de_0_9_1_saida));  // open: MODE
endmodule

module REGISTRADOR_0_9 (
  input  CLK,
  input  [3:0] ENTRADA_4BITS,
  input  RESET,
  input  PRESET,
  output [3:0] \SAÍDA_4BITS 
);

  wire or_1_out, or_2_out;

  D_Flip_Flop d_ff_1 (
    .clk(CLK), .D(ENTRADA_4BITS[3]), .Q(\SAÍDA_4BITS [3]), .preset(PRESET), .reset(RESET));  // open: Qn, en
  D_Flip_Flop d_ff_2 (.clk(CLK), .D(ENTRADA_4BITS[2]), .Q(\SAÍDA_4BITS [2]), .reset(or_1_out));  // open: Qn, preset, en
  or or_1 (or_1_out, RESET, PRESET);
  D_Flip_Flop d_ff_3 (.clk(CLK), .D(ENTRADA_4BITS[1]), .Q(\SAÍDA_4BITS [1]), .reset(or_2_out));  // open: Qn, preset, en
  or or_2 (or_2_out, RESET, PRESET);
  D_Flip_Flop d_ff_4 (
    .clk(CLK), .D(ENTRADA_4BITS[0]), .Q(\SAÍDA_4BITS [0]), .preset(PRESET), .reset(RESET));  // open: Qn, en
endmodule

module CONTADOR_0_5 (
  input  CLK,
  input  RESET,
  input  MODE,
  output [3:0] SAIDA,
  output CLK_SEGUINTE
);

  wire and_1_out, not_1_out;
  wire [3:0] adder_1_out;

  REGISTRADOR_0_5 registrador_0_5_1 (
    .CLK(CLK), .ENTRADA_4BITS(adder_1_out), .RESET(RESET), .PRESET(and_1_out), .\SAÍDA_4BITS (SAIDA));
  Hex_Digit_Display hex_digit_display_1 (.value(SAIDA));  // open: dp
  Adder #(.width(4)) adder_1 (.a(SAIDA), .b(4'b1111), .out(adder_1_out));  // open: cin, cout
  and and_1 (and_1_out, SAIDA[0], SAIDA[1], SAIDA[2], SAIDA[3]);
  and and_2 (CLK_SEGUINTE, and_1_out, not_1_out);
  not not_1 (not_1_out, MODE);
endmodule

module ADAWD (
  input  CLK,
  input  RESET,
  input  [3:0] in_3,
  output [3:0] SAIDA,
  output CLOCK_SEGUINTE
);

  wire or_1_out;
  wire [3:0] adder_1_out, multiplexer_1_out, undriven;

  or or_1 (or_1_out, CLOCK_SEGUINTE, RESET);
  REGISTRADOR_0_9 REGISTRADOR (
    .CLK(CLK), .RESET(or_1_out), .ENTRADA_4BITS(adder_1_out), .\SAÍDA_4BITS (SAIDA),
    .PRESET(multiplexer_1_out[0]));
  Hex_Digit_Display hex_digit_display_1 (.value(SAIDA));  // open: dp
  Adder #(.width(4)) adder_1 (.a(SAIDA), .b(4'b0001), .out(adder_1_out));  // open: cin, cout
  Multiplexer #(.width(4)) multiplexer_1 (.in0(undriven), .in1(in_3), .out(multiplexer_1_out));  // open: sel, en
  and and_1 (CLOCK_SEGUINTE, SAIDA[0], SAIDA[1], SAIDA[2], SAIDA[3]);
  // Pins of 1 and 4 bits meet at multiplexer_1_out
endmodule

module REGISTRADOR_0_5 (
  input  CLK,
  input  [3:0] ENTRADA_4BITS,
  input  RESET,
  input  PRESET,
  output [3:0] \SAÍDA_4BITS 
);

  wire or_1_out, or_2_out;

  or or_1 (or_1_out, PRESET, RESET);
  D_Flip_Flop d_ff_1 (.clk(CLK), .D(ENTRADA_4BITS[3]), .Q(\SAÍDA_4BITS [3]), .reset(or_1_out));  // open: Qn, preset, en
  D_Flip_Flop d_ff_2 (
    .clk(CLK), .D(ENTRADA_4BITS[2]), .Q(\SAÍDA_4BITS [2]), .preset(PRESET), .reset(RESET));  // open: Qn, en
  D_Flip_Flop d_ff_3 (.clk(CLK), .D(ENTRADA_4BITS[1]), .Q(\SAÍDA_4BITS [1]), .reset(or_2_out));  // open: Qn, preset, en
  or or_2 (or_2_out, PRESET, RESET);
  D_Flip_Flop d_ff_4 (
    .clk(CLK), .D(ENTRADA_4BITS[0]), .Q(\SAÍDA_4BITS [0]), .preset(PRESET), .reset(RESET));  // open: Qn, en
endmodule

module CRONOMETRO (
  input  PAUSE,
  input  RESET,
  input  MODE,
  input  CLOCK_PRINCIPAL,
  input  dm,
  input  um,
  input  ds,
  input  us,
  output [3:0] DM_2,
  output [3:0] UM_2,
  output [3:0] DS_2,
  output [3:0] US_2,
  output END
);

  wire and_1_out, and_2_out, and_3_out, and_4_out, and_5_out, and_6_out, and_7_out, and_8_out, and_9_out,
       and_10_out, CLOCK_PRINCIPAL_out, contador_0_5_2_clk_seguinte, contador_de_0_9_1_clock_seguinte,
       contador_de_0_9_2_clock_seguinte, dm_out, ds_out, not_1_out, not_2_out, not_3_out, not_4_out,
       not_5_out, not_6_out, not_7_out, not_8_out, not_9_out, not_10_out, not_11_out, not_12_out, not_13_out,
       not_14_out, not_15_out, not_16_out, not_17_out, or_1_out, or_2_out, or_3_out, or_4_out, um_out, us_out;

  Hex_Digit_Display hex_digit_display_1 (.value(DM_2));  // open: dp
  Hex_Digit_Display hex_digit_display_2 (.value(UM_2));  // open: dp
  Hex_Digit_Display hex_digit_display_3 (.value(DS_2));  // open: dp
  Button u_dm (.out(dm_out));
  Button u_um (.out(um_out));
  Button u_ds (.out(ds_out));
  Button u_us (.out(us_out));
  Hex_Digit_Display hex_digit_display_4 (.value(US_2));  // open: dp
  and and_1 (and_1_out, not_3_out, not_4_out, not_2_out, not_1_out);
  not not_1 (not_1_out, DM_2[0]);
  not not_2 (not_2_out, DM_2[1]);
  not not_3 (not_3_out, DM_2[3]);
  not not_4 (not_4_out, DM_2[2]);
  CONTADOR_0_5 contador_0_5_1 (.CLK(or_1_out), .RESET(RESET), .SAIDA(DM_2), .MODE(MODE));  // open: CLK_SEGUINTE
  and and_2 (and_2_out, not_5_out, not_6_out, not_8_out, not_7_out);
  not not_5 (not_5_out, UM_2[3]);
  not not_6 (not_6_out, UM_2[2]);
  not not_7 (not_7_out, UM_2[0]);
  not not_8 (not_8_out, UM_2[1]);
  or or_1 (or_1_out, and_4_out, contador_de_0_9_1_clock_seguinte);
  and and_3 (and_3_out, MODE, um);
  and and_4 (and_4_out, MODE, dm);
  and and_5 (and_5_out, not_10_out, not_9_out, not_12_out, not_11_out);
  not not_9 (not_9_out, DS_2[2]);
  not not_10 (not_10_out, DS_2[3]);
  CONTADOR_DE_0_9 contador_de_0_9_1 (
    .CLK(or_2_out), .RESET(RESET), .CLOCK_SEGUINTE(contador_de_0_9_1_clock_seguinte), .SAIDA(UM_2),
    .MODE(MODE));
  or or_2 (or_2_out, and_3_out, contador_0_5_2_clk_seguinte);
  not not_11 (not_11_out, DS_2[0]);
  not not_12 (not_12_out, DS_2[1]);
  or or_3 (or_3_out, and_6_out, contador_de_0_9_2_clock_seguinte);
  and and_6 (and_6_out, MODE, ds);
  and and_7 (and_7_out, not_13_out, not_15_out, not_14_out, not_16_out);
  not not_13 (not_13_out, US_2[3]);
  not not_14 (not_14_out, US_2[1]);
  not not_15 (not_15_out, US_2[2]);
  not not_16 (not_16_out, US_2[0]);
  CONTADOR_0_5 contador_0_5_2 (
    .CLK(or_3_out), .CLK_SEGUINTE(contador_0_5_2_clk_seguinte), .RESET(RESET), .SAIDA(DS_2), .MODE(MODE));
  CONTADOR_DE_0_9 contador_de_0_9_2 (
    .CLK(or_4_out), .RESET(RESET), .CLOCK_SEGUINTE(contador_de_0_9_2_clock_seguinte), .SAIDA(US_2),
    .MODE(MODE));
  or or_4 (or_4_out, and_8_out, and_10_out);
  and and_8 (and_8_out, MODE, us);
  and and_9 (and_9_out, and_7_out, and_5_out, and_2_out, and_1_out);
  and and_10 (and_10_out, CLOCK_PRINCIPAL, not_17_out);
  or or_5 (END, and_9_out, PAUSE);
  Clock u_CLOCK_PRINCIPAL (.out(CLOCK_PRINCIPAL_out));
  not not_17 (not_17_out, END);
endmodule

module CRON_TESTE (
  input  RESET,
  input  MODE,
  output [3:0] DM,
  output [3:0] UM,
  output [3:0] DS,
  output [3:0] US
);

  wire CLOCK_PRINCIPAL_out, contador_0_5_2_p3, contador_de_0_9_1_clock_seguinte,
       contador_de_0_9_2_clock_seguinte, dm_out, ds_out, or_1_out, or_2_out, or_3_out, or_4_out, um_out,
       us_out;

  Hex_Digit_Display hex_digit_display_1 (.value(DM));  // open: dp
  Hex_Digit_Display hex_digit_display_2 (.value(UM));  // open: dp
  Hex_Digit_Display hex_digit_display_3 (.value(DS));  // open: dp
  Hex_Digit_Display hex_digit_display_4 (.value(US));  // open: dp
  or or_1 (or_1_out, contador_de_0_9_1_clock_seguinte, dm_out);
  // CONTADOR_0_5 contador_0_5_1: pin names not known; wires that end beside it: or_1_out, DM, RESET, MODE
  Button u_dm (.out(dm_out));
  CONTADOR_DE_0_9 contador_de_0_9_1 (
    .CLK(or_2_out), .RESET(RESET), .CLOCK_SEGUINTE(contador_de_0_9_1_clock_seguinte), .SAIDA(UM));  // open: MODE
  or or_2 (or_2_out, contador_0_5_2_p3, um_out);
  Button u_um (.out(um_out));
  or or_3 (or_3_out, contador_de_0_9_2_clock_seguinte, ds_out);
  // CONTADOR_0_5 contador_0_5_2: pin names not known; wires that end beside it: or_3_out, DS, contador_0_5_2_p3, RESET, MODE
  Button u_ds (.out(ds_out));
  CONTADOR_DE_0_9 contador_de_0_9_2 (
    .CLK(or_4_out), .RESET(RESET), .CLOCK_SEGUINTE(contador_de_0_9_2_clock_seguinte), .SAIDA(US));  // open: MODE
  or or_4 (or_4_out, us_out, CLOCK_PRINCIPAL_out);
  Button u_us (.out(us_out));
  Clock CLOCK_PRINCIPAL (.out(CLOCK_PRINCIPAL_out));
endmodule

module TESTE_CHUT (
  input  [3:0] in_1,
  input  CHUTAR,
  input  MUDAR_ESTADO,
  output [3:0] Y,
  output [3:0] X,
  output RESULTADO,
  output CHUTANDO_Y,
  output CHUTANDO_X
);

  wire and_1_out, and_3_out;
  wire [1:0] counter_1_q;

  Counter #(.width(2), .max('h2)) counter_1 (.Q(counter_1_q), .clk(MUDAR_ESTADO));  // open: load, D, count, carry, clr
  and and_1 (and_1_out, CHUTAR, CHUTANDO_Y);
  and and_2 (CHUTANDO_Y, ~counter_1_q[1], counter_1_q[0]);  // AND_Gate
  Register #(.width(4)) register_1 (.D(in_1), .Q(Y), .clk(and_1_out));  // open: en, clr
  Register #(.width(4)) register_2 (.D(in_1), .Q(X), .clk(and_3_out));  // open: en, clr
  and and_3 (and_3_out, CHUTAR, CHUTANDO_X);
  and and_4 (CHUTANDO_X, ~counter_1_q[1], ~counter_1_q[0]);  // AND_Gate
  and and_5 (RESULTADO, counter_1_q[1], ~counter_1_q[0]);  // AND_Gate
endmodule

module TABELA_VERDADE (
  input  a,
  input  c,
  input  e,
  input  f,
  output saida,
  output h,
  output i,
  output j,
  output k
);

  wire and_1_out, and_2_out, and_3_out, and_4_out, and_5_out, and_6_out, and_7_out, not_1_out, not_2_out,
       not_3_out, not_4_out, not_5_out, not_6_out, not_7_out, not_8_out, not_9_out, not_10_out, not_11_out;

  not not_1 (not_1_out, c);
  not not_2 (not_2_out, e);
  not not_3 (not_3_out, f);
  not not_4 (not_4_out, a);
  and and_1 (and_1_out, not_4_out, c);
  not not_5 (not_5_out, e);
  and and_2 (and_2_out, c, not_5_out, not_6_out);
  not not_6 (not_6_out, f);
  and and_3 (and_3_out, a, not_7_out, f);
  not not_7 (not_7_out, c);
  not not_8 (not_8_out, c);
  and and_4 (and_4_out, a, not_8_out, e);
  not not_9 (not_9_out, a);
  and and_5 (and_5_out, not_9_out, e);
  and and_6 (and_6_out, e, not_10_out);
  not not_10 (not_10_out, f);
  not not_11 (not_11_out, e);
  and and_7 (and_7_out, a, not_11_out, f);
  and and_8 (h, a, not_1_out, not_2_out, not_3_out);
  or or_1 (i, and_1_out, and_2_out, and_3_out, and_4_out);
  or or_2 (j, and_5_out, and_6_out, and_7_out);

  assign k = f;
  assign saida = a;
endmodule

module TESTE_CHUTE (
  input  in_1,
  input  in_2,
  input  in_3,
  input  in_4
);

  wire tabela_verdade_1_saida;
  wire [3:0] tabela_verdade_1_k;

  TABELA_VERDADE tabela_verdade_1 (
    .a(in_1), .c(in_2), .e(in_3), .f(in_4), .saida(tabela_verdade_1_saida), .h(tabela_verdade_1_k[3]),
    .i(tabela_verdade_1_k[2]), .j(tabela_verdade_1_k[1]), .k(tabela_verdade_1_k[0]));
  _7_Segment_Display u_7_segment_display_1 (.g(tabela_verdade_1_saida));  // open: f, a, b, e, d, c, dp
  Hex_Digit_Display hex_digit_display_1 (.value(tabela_verdade_1_k));  // open: dp
endmodule

module memoria (
  input  in_1,
  input  [3:0] in_2,
  input  RESET,
  output [3:0] out_4
);

  D_Flip_Flop d_ff_1 (.clk(in_1), .D(in_2[3]), .Q(out_4[3]), .reset(RESET));  // open: Qn, preset, en
  D_Flip_Flop d_ff_2 (.clk(in_1), .D(in_2[2]), .Q(out_4[2]), .reset(RESET));  // open: Qn, preset, en
  D_Flip_Flop d_ff_3 (.clk(in_1), .D(in_2[1]), .Q(out_4[1]), .reset(RESET));  // open: Qn, preset, en
  D_Flip_Flop d_ff_4 (.clk(in_1), .D(in_2[0]), .Q(out_4[0]), .reset(RESET));  // open: Qn, preset, en
endmodule

// CORE
module CORE_2 (
  input  A,
  input  A2,
  input  A3,
  input  A4,
  input  B,
  input  B2,
  input  B3,
  input  B4,
  input  MUDAR_ESTADO,
  input  CLOCK,
  input  RESET,
  output B_JOG,
  output CHUTANDO_Y,
  output CHUTANDO_X,
  output A_JOG,
  output NEG_B,
  output [3:0] SLA_B,
  output NEG_A,
  output [3:0] SLA_A,
  output MAIOR,
  output IGUAL_SOMA,
  output MENOR,
  output IGUAL_CORDS,
  output ACERTOU,
  output B_GANHOU,
  output [3:0] PLACAR_B,
  output EMPATE,
  output [3:0] PLACAR_A,
  output A_GANHOU
);

  wire and_1_out, and_2_out, comparator_1_eq, comparator_2_eq, not_2_out, teste_chut_1_resultado;
  wire [3:0] memoria_1_out_4, memoria_2_out_4, multiplexer_1_out, teste_chut_1_x, teste_chut_1_y;

  not not_1 (A_JOG, B_JOG);
  _7_Segment_Display u_7_segment_display_1 (.g(NEG_A));  // open: f, a, b, e, d, c, dp
  and and_1 (and_1_out, ACERTOU, B_JOG);
  T_Flip_Flop #(.trigger("falling")) t_ff_1 (
    .clk(teste_chut_1_resultado), .T(1'b1), .Q(B_JOG));  // open: Qn, preset, reset, en
  memoria memoria_1 (.in_1(not_2_out), .in_2(teste_chut_1_x), .RESET(RESET), .out_4(memoria_1_out_4));
  TABELA_VERDADE tabela_verdade_1 (
    .a(memoria_1_out_4[3]), .c(memoria_1_out_4[2]), .e(memoria_1_out_4[1]), .f(memoria_1_out_4[0]),
    .saida(NEG_A), .h(SLA_A[3]), .i(SLA_A[2]), .j(SLA_A[1]), .k(SLA_A[0]));
  Hex_Digit_Display hex_digit_display_1 (.value(SLA_A));  // open: dp
  and and_2 (and_2_out, ACERTOU, A_JOG);
  not not_2 (not_2_out, CLOCK);
  Counter #(.width(4), .max('ha)) counter_1 (.Q(PLACAR_B), .clk(and_1_out));  // open: load, D, count, carry, clr
  Hex_Digit_Display hex_digit_display_2 (.value(PLACAR_B));  // open: dp
  Counter #(.width(4), .max('ha)) counter_2 (.Q(PLACAR_A), .clk(and_2_out));  // open: load, D, count, carry, clr
  Hex_Digit_Display hex_digit_display_3 (.value(PLACAR_A));  // open: dp
  Multiplexer #(.width(4), .enable("false")) multiplexer_1 (
    .in0({A, A2, A3, A4}), .in1({B, B2, B3, B4}), .out(multiplexer_1_out), .sel(B_JOG));
  TESTE_CHUT teste_chut_1 (
    .in_1(multiplexer_1_out), .CHUTAR(CLOCK), .MUDAR_ESTADO(MUDAR_ESTADO), .Y(teste_chut_1_y),
    .X(teste_chut_1_x), .RESULTADO(teste_chut_1_resultado), .CHUTANDO_Y(CHUTANDO_Y), .CHUTANDO_X(CHUTANDO_X));
  _7_Segment_Display u_7_segment_display_2 (.g(NEG_B));  // open: f, a, b, e, d, c, dp
  COMPARADOR_SOMA comparador_soma_1 (
    .in_1(teste_chut_1_resultado), .ENTRADA_X(memoria_1_out_4), .ENTRADA_Y(memoria_2_out_4), .MAIOR(MAIOR),
    .IGUAL_SOMA(IGUAL_SOMA), .MENOR(MENOR), .IGUAL_CORDS(ACERTOU));  // open: MUDAR_CORDS
  memoria memoria_2 (.in_1(not_2_out), .in_2(teste_chut_1_y), .RESET(RESET), .out_4(memoria_2_out_4));
  TABELA_VERDADE tabela_verdade_2 (
    .a(memoria_2_out_4[3]), .c(memoria_2_out_4[2]), .e(memoria_2_out_4[1]), .f(memoria_2_out_4[0]),
    .saida(NEG_B), .h(SLA_B[3]), .i(SLA_B[2]), .j(SLA_B[1]), .k(SLA_B[0]));
  Hex_Digit_Display hex_digit_display_4 (.value(SLA_B));  // open: dp
  Comparator #(.width(4)) comparator_1 (.a(PLACAR_B), .b(PLACAR_A), .gt(B_GANHOU), .eq(comparator_1_eq));  // open: lt
  Comparator #(.width(4)) comparator_2 (.a(PLACAR_A), .b(PLACAR_B), .gt(A_GANHOU), .eq(comparator_2_eq));  // open: lt
  and and_3 (EMPATE, comparator_1_eq, comparator_2_eq);

  assign IGUAL_CORDS = ACERTOU;

  // Notes on the sheet:
  //   JOGADOR 0
  //   EIXO X
  //   EIXO Y
  //   JOGADOR 1
endmodule

module MUDADOR_DE_EIXOS (
  input  CHUTAR
);

  wire [1:0] adder_1_out, d_ff_2_q;
  wire [2:0] and_1_out, multiplexer_1_out;

  D_Flip_Flop d_ff_1 (.clk(CHUTAR), .D(adder_1_out[1]), .Q(d_ff_2_q[1]));  // open: Qn, preset, en, reset
  D_Flip_Flop d_ff_2 (.clk(CHUTAR), .D(adder_1_out[0]), .Q(d_ff_2_q[0]));  // open: Qn, preset, en, reset
  Adder #(.width(2)) adder_1 (.a(d_ff_2_q), .b(2'b01), .out(adder_1_out));  // open: cin, cout
  and and_1 (and_1_out[0], ~adder_1_out[1], adder_1_out[0]);  // AND_Gate
  and and_2 (and_1_out[1], adder_1_out[1], ~adder_1_out[0]);  // AND_Gate
  and and_3 (and_1_out[2], adder_1_out[1], adder_1_out[0]);
  Multiplexer #(.width(3)) multiplexer_1 (.in0(and_1_out), .out(multiplexer_1_out));  // open: in1, sel, en
endmodule

module COMPARADOR_SOMA (
  input  in_1,
  input  [3:0] ENTRADA_X,
  input  [3:0] ENTRADA_Y,
  input  MUDAR_CORDS,
  output MAIOR,
  output IGUAL_SOMA,
  output MENOR,
  output IGUAL_CORDS
);

  wire and_1_out, clock_1_out, comparator_1_eq, comparator_1_gt, comparator_1_lt, comparator_2_eq,
       comparator_3_eq, counter_1_carry;
  wire [4:0] adder_1_out, adder_2_out, bit_extender_1_out, bit_extender_2_out, bit_extender_3_out,
       bit_extender_4_out;
  wire [7:0] random_1_out;

  Clock clock_1 (.out(clock_1_out));
  Counter #(.width(4), .max('ha)) counter_1 (
    .carry(counter_1_carry), .clk(and_1_out), .clr(counter_1_carry));  // open: load, D, count, Q
  and and_1 (and_1_out, clock_1_out, IGUAL_CORDS);
  Random random_1 (.clk(counter_1_carry), .out(random_1_out));  // open: next, clr
  assign bit_extender_1_out = {{1{ENTRADA_X[3]}}, ENTRADA_X};  // Bit_Extender bit_extender_1
  assign bit_extender_2_out = {{1{ENTRADA_Y[3]}}, ENTRADA_Y};  // Bit_Extender bit_extender_2
  Adder #(.width(5)) adder_1 (.a(bit_extender_1_out), .b(bit_extender_2_out), .out(adder_1_out));  // open: cin, cout
  assign bit_extender_3_out = {{1{random_1_out[3]}}, random_1_out[3:0]};  // Bit_Extender bit_extender_3
  assign bit_extender_4_out = {{1{random_1_out[7]}}, random_1_out[7:4]};  // Bit_Extender bit_extender_4
  Adder #(.width(5)) adder_2 (.a(bit_extender_3_out), .b(bit_extender_4_out), .out(adder_2_out));  // open: cin, cout
  Comparator #(.width(5)) comparator_1 (
    .a(adder_1_out), .b(adder_2_out), .gt(comparator_1_gt), .eq(comparator_1_eq), .lt(comparator_1_lt));
  and and_2 (MAIOR, in_1, comparator_1_gt);
  and and_3 (IGUAL_SOMA, in_1, comparator_1_eq);
  and and_4 (MENOR, in_1, comparator_1_lt);
  Comparator #(.width(4)) comparator_2 (.a(random_1_out[3:0]), .b(ENTRADA_X), .eq(comparator_2_eq));  // open: gt, lt
  Comparator #(.width(4)) comparator_3 (.a(random_1_out[7:4]), .b(ENTRADA_Y), .eq(comparator_3_eq));  // open: gt, lt
  and and_5 (IGUAL_CORDS, comparator_2_eq, in_1, comparator_3_eq);

  // Notes on the sheet:
  //   x
  //   y
  //   y
endmodule
